# Fritzing sketch filament maker - fritzing (saved by Fritzing 1.0.1rc)

parts:
  Деталь1 = Arduino Nano (Rev3.0)
  Motor-Active-LED = LED - 3mm [color="Blue (505nm)" current=0.030A package="3 mm [THT]"]
  Start-Stop-Motor = Square Pushbutton
  ENCODER1 = Rotary Encoder with Knob
  Motor-Direction-Switch = Taiway 100-SP-X-T1 SPDT Miniature Toggle Switch [part_number=100-SP-X-T1-0-0-B1-M1 package=THT]
  R1 = Temperature Sensor (Thermistor) [thermistor_type=NTC part_number="NTC 100K" package=THT]
  Motor = Stepper Motor - Bipolar
  Pololu_A1 = Pololu A4988 [package=SO16]
  Filament-End-Sensor = D2F-FL Omron Snap Action Limit Switch with Level
  Q1-Fan-Mosfet = MOSFET-NCHANNEL [part_number="Any simple MOSFET" package=to220v]
  Q2-Heater-Mosfet = MOSFET-NCHANNEL [part_number=IRLZ44N package=to220v]
  Fan-LED = LED - 3mm [color="Green (555nm)" current=0.030A package="3 mm [THT]"]
  Heater-LED = LED - 3mm [color="Red (635nm)" current=0.030A package="3 mm [THT]"]
  C2 = Electrolytic Capacitor [capacitance=200µF voltage=16V package="200 mil [THT, electrolytic]"]
  Heater = Inductor [part_number=40W-12V package="400 mil [THT]"]
  ATX_250-300W = ATX24 Pin Power Supply Connector [package=atx24_right_angle]
  ON-OFF = SWITCH-SPST-2 [package=switch-spst-vertical]
  LCD3 = LCD screen
  LCM1602_IIC3 = LCM1602 IIC [part_number="LCM1602 IIC" chip_label="LCM1602 IIC" package="DIP (Dual Inline) [THT]"]
  C3 = Electrolytic Capacitor [capacitance=10µF voltage=16V package="200 mil [THT, electrolytic]"]
  Filament-Cooling-FAN = Fan - Ventilador [part_number=12V package=THT]
  R4 = Resistor [tolerance=±5% resistance=10k power=0.25W package=THT]
  R2 = Resistor [tolerance=±5% resistance=220 power=0.25W package=THT]
  R8 = Resistor [tolerance=±5% resistance=10k power=0.25W package=THT]
  R11 = Resistor [tolerance=±5% resistance=10 power=0.25W package=THT]
  R10 = Resistor [tolerance=±5% resistance=10 power=0.25W package=THT]
  R9 = Resistor [tolerance=±5% resistance=10k power=0.25W package=THT]
  R5 = Resistor [tolerance=±5% resistance=4.7k power=0.25W package=THT]
  R3 = Resistor [tolerance=±5% resistance=10k power=0.25W package=THT]
  R6 = Resistor [tolerance=±5% resistance=1.8k power=0.25W package=THT]
  R7 = Resistor [tolerance=±5% resistance=1.8k power=0.25W package=THT]
  R12 = Resistor [tolerance=±5% resistance=10k power=0.25W package=THT]

nets:
  GND: Деталь1.GND, Start-Stop-Motor.leg1, ENCODER1.no_name_yet#3, ENCODER1.no_name_yet#5, Motor-Direction-Switch.L2, R1.pin_1, Pololu_A1.GND, Filament-End-Sensor.Pin_2, Q1-Fan-Mosfet.S, Q2-Heater-Mosfet.S, C2.-, ATX_250-300W.GND, ON-OFF.P, C3.-, R2.Pin_1, R8.Pin_1, R9.Pin_1
  N1: Деталь1.D2, Pololu_A1.ENABLE, R12.Pin_0
  N2: Деталь1.D3, R10.Pin_1
  N3: Деталь1.D4, Pololu_A1.DIR
  N4: Деталь1.D5, Pololu_A1.STEP
  N5: Деталь1.D6, R11.Pin_1
  N6: Деталь1.D7, Start-Stop-Motor.leg0
  N7: Деталь1.D8, ENCODER1.no_name_yet#2, R4.Pin_1
  N8: Деталь1.D9, ENCODER1.no_name_yet#1, R3.Pin_1
  N9: Деталь1.D10, Motor-Direction-Switch.COM
  N10: Деталь1.D11/MOSI, ENCODER1.no_name_yet#4
  N11: Деталь1.D12/MISO, Pololu_A1.MS1, Pololu_A1.MS2, Pololu_A1.MS3
  5V: Деталь1.5V, Pololu_A1.VDD, ATX_250-300W.5V, R4.Pin_0, R5.Pin_0, R3.Pin_0, R12.Pin_1
  N12: Деталь1.A5, LCM1602_IIC3.SCL
  N13: Деталь1.A4, LCM1602_IIC3.SDA
  N14: Деталь1.A2, Filament-End-Sensor.Pin_3
  N15: Деталь1.A0, R1.pin_0, C3.+, R5.Pin_1
  N16: Деталь1.D13/SCK, Motor-Active-LED.anode
  N17: Motor-Active-LED.cathode, R2.Pin_0
  N18: Motor.A, Pololu_A1.2B
  N19: Motor.C, Pololu_A1.2A
  N20: Motor.B, Pololu_A1.1A
  N21: Motor.D, Pololu_A1.1B
  N22: Pololu_A1.RESET, Pololu_A1.SLEEP
  12V: Pololu_A1.VMOT, C2.+, Heater.pin_0, ATX_250-300W.12V, Filament-Cooling-FAN.5V, R6.Pin_1, R7.Pin_1
  N23: Q1-Fan-Mosfet.G, R8.Pin_0, R11.Pin_0
  N24: Q1-Fan-Mosfet.D, Fan-LED.cathode, Filament-Cooling-FAN.GND
  N25: Q2-Heater-Mosfet.G, R10.Pin_0, R9.Pin_0
  N26: Q2-Heater-Mosfet.D, Heater-LED.cathode, Heater.pin_1
  N27: Fan-LED.anode, R7.Pin_0
  N28: Heater-LED.anode, R6.Pin_0
  N29: ATX_250-300W.PS_ON, ON-OFF.O
  VSS: LCD3.VSS, LCM1602_IIC3.VSS
  VDD: LCD3.VDD, LCM1602_IIC3.VDD
  N30: LCD3.V0, LCM1602_IIC3.V0
  N31: LCD3.RS, LCM1602_IIC3.RS
  N32: LCD3.R/W, LCM1602_IIC3.RW
  N33: LCD3.E, LCM1602_IIC3.E
  N34: LCD3.DB0, LCM1602_IIC3.D0
  N35: LCD3.DB1, LCM1602_IIC3.D1
  N36: LCD3.DB2, LCM1602_IIC3.D2
  N37: LCD3.DB3, LCM1602_IIC3.D3
  N38: LCD3.DB4, LCM1602_IIC3.D4
  N39: LCD3.DB5, LCM1602_IIC3.D5
  N40: LCD3.DB6, LCM1602_IIC3.D6
  N41: LCD3.DB7, LCM1602_IIC3.D7
  N42: LCD3.LED+, LCM1602_IIC3.A
  N43: LCD3.LED-, LCM1602_IIC3.K
  N44: LCM1602_IIC3.LED_A, LCM1602_IIC3.LED_B

custom parts:
  Rotary Encoder with Knob: Rotary Encoder with 1/4" Shaft and Knob
  D2F-FL Omron Snap Action Limit Switch with Level: Snap action switch with stainless steel lever.
  LCM1602 IIC: I2C-Module to use a 1602 or 2004 LCD on with the wire.h libory Serial LCD Modul
  Fan - Ventilador: Ventilador de 2 pines, se encuentra comunmente en computadoras de escritorio
